# Fritzing sketch BaseSketch (saved by Fritzing 0.9.10b)
breadboards: 1

parts:
  Bauteil2 = Arduino Uno (Rev3)
  GY-NEO6MV3 = SUP500F [package=sup500f]
  R3 = Resistor [tolerance=±5% resistance=4.7k package="1206 [SMD]"]
  R4 = Resistor [tolerance=±5% resistance=10k package="1206 [SMD]"]

nets:
  N1: Bauteil2.D3_PWM, GY-NEO6MV3.VCC
  N2: Bauteil2.D4, R3.Pin_0
  N3: Bauteil2.5V, GY-NEO6MV3.TX-O
  N4: Bauteil2.GND, GY-NEO6MV3.RX-I, R4.Pin_1
  N5: GY-NEO6MV3.GND, R3.Pin_1, R4.Pin_0

notes:
  GND: Black
  VCC: Red
  RX: Yellow
  TX: Green
  https://arduinogetstarted.com/tutorials/arduino-gps

// code stored in the sketch: main.ino
/*
 * Created by ArduinoGetStarted.com
 *
 * This example code is in the public domain
 *
 * Tutorial page: https://arduinogetstarted.com/tutorials/arduino-gps
 */

#include <TinyGPS++.h>
#include <SoftwareSerial.h>

const int RXPin = 3, TXPin = 4;
const uint32_t GPSBaud = 9600; //Default baud of NEO-6M is 9600


TinyGPSPlus gps; // the TinyGPS++ object
SoftwareSerial gpsSerial(RXPin, TXPin); // the serial interface to the GPS device

void setup() {
  Serial.begin(9600);
  gpsSerial.begin(GPSBaud);

  Serial.println(F("Arduino - GPS module"));
}

void loop() {
  if (gpsSerial.available() > 0) {
    if (gps.encode(gpsSerial.read())) {
      if (gps.location.isValid()) {
        Serial.print(F("- latitude: "));
        Serial.println(gps.location.lat());

        Serial.print(F("- longitude: "));
        Serial.println(gps.location.lng());

        Serial.print(F("- altitude: "));
        if (gps.altitude.isValid())
          Serial.println(gps.altitude.meters());
        else
          Serial.println(F("INVALID"));
      } else {
        Serial.println(F("- location: INVALID"));
      }

      Serial.print(F("- speed: "));
      if (gps.speed.isValid()) {
        Serial.print(gps.speed.kmph());
        Serial.println(F(" km/h"));
      } else {
        Serial.println(F("INVALID"));
      }

      Serial.print(F("- GPS date&time: "));
      if (gps.date.isValid() && gps.time.isValid()) {
        Serial.print(gps.date.year());
        Serial.print(F("-"));
        Serial.print(gps.date.month());
        Serial.print(F("-"));
        Serial.print(gps.date.day());
        Serial.print(F(" "));
        Serial.print(gps.time.hour());
        Serial.print(F(":"));
        Serial.print(gps.time.minute());
        Serial.print(F(":"));
        Serial.println(gps.time.second());
      } else {
        Serial.println(F("INVALID"));
      }

      Serial.println();
    }
  }

  if (millis() > 5000 && gps.charsProcessed() < 10)
    Serial.println(F("No GPS data received: check wiring"));
}
